// Logisim project RegInit.circ as structural Verilog: 1 circuit, main circuit main
module main (
  input  [7:0] in_1,
  output [7:0] out_2
);

  wire and_2_out, clk, comparator_2_eq, comparator_3_eq, f;
  wire [7:0] a1, a2, a3, and_1_out, multiplexer_1_out, multiplexer_2_out, multiplexer_3_out, res, \time ;

  Counter counter_1 (.Q(\time ), .clk(clk));  // open: load, D, count, carry, clr
  Clock clock_1 (.out(clk));
  Comparator comparator_1 (.a(\time ), .b({8{1'b0}}), .eq(f));  // open: gt, lt
  // Probe on res
  Adder adder_1 (.a(a3), .b(and_1_out), .out(res));  // open: cin, cout
  assign and_1_out = a2 & a1;  // AND_Gate and_1, 8 bits wide
  Multiplexer #(.width(8)) multiplexer_1 (.in0(res), .in1(8'h1), .out(multiplexer_1_out), .sel(f));  // open: en
  Register u_a3 (.D(multiplexer_1_out), .Q(a3), .clk(clk));  // open: en, clr
  Register u_a2 (.D(multiplexer_2_out), .Q(a2), .clk(clk));  // open: en, clr
  Multiplexer #(.width(8)) multiplexer_2 (.in0(a3), .in1(8'h1), .out(multiplexer_2_out), .sel(f));  // open: en
  Multiplexer #(.width(8)) multiplexer_3 (.in0(a2), .in1({8{1'b0}}), .out(multiplexer_3_out), .sel(f));  // open: en
  Register u_a1 (.D(multiplexer_3_out), .Q(a1), .clk(clk));  // open: en, clr
  Comparator comparator_2 (.a(in_1), .b(\time ), .eq(comparator_2_eq));  // open: gt, lt
  and and_2 (and_2_out, comparator_2_eq, comparator_3_eq);
  Register a2_2 (.D(a2), .en(and_2_out), .Q(out_2), .clk(clk));  // open: clr
  Comparator comparator_3 (.a({8{1'b0}}), .b(out_2), .eq(comparator_3_eq));  // open: gt, lt

  // Other names for the same wires on the sheet: n[7:0] = in_1
endmodule
