// Logisim project fsm_p0.circ as structural Verilog
module nextStateLogic (
  input  [1:0] State,
  input  [1:0] IN,
  output [1:0] next
);

  next next_1 (.S1(State[1]), .S0(State[0]), .IN1(IN[1]), .ss1(next[1]), .IN0(IN[0]), .ss0(next[0]));
endmodule

module fsm (
  input  CLR,
  input  [1:0] In,
  output Z
);

  wire clock_1_out;
  wire [1:0] multiplexer_1_out, nextstatelogic_1_next, state;

  nextStateLogic nextstatelogic_1 (.State(state), .IN(In), .next(nextstatelogic_1_next));
  Multiplexer #(.width(2), .enable("false")) multiplexer_1 (
    .in0(nextstatelogic_1_next), .in1(2'b00), .out(multiplexer_1_out), .sel(CLR));
  Clock clock_1 (.out(clock_1_out));
  Register #(.width(2)) register_1 (.D(multiplexer_1_out), .Q(state), .clk(clock_1_out));  // open: en, clr
  \output  output_1 (.State(state), .IN(In), .out_3(Z));
endmodule

module next (
  input  S1,
  input  S0,
  input  IN1,
  input  IN0,
  output ss1,
  output ss0
);

  wire and_1_out, and_2_out, and_3_out, and_4_out, and_5_out, and_6_out, and_7_out, and_8_out, not_1_out,
       not_2_out, not_3_out, not_4_out, not_5_out, not_6_out, not_7_out, not_8_out, not_9_out, not_10_out,
       not_11_out, not_12_out, not_13_out, not_14_out, not_15_out, not_16_out;

  not not_1 (not_1_out, S1);
  and and_1 (and_1_out, not_1_out, S0, not_2_out);
  not not_2 (not_2_out, IN1);
  not not_3 (not_3_out, S1);
  and and_2 (and_2_out, not_3_out, S0, not_4_out);
  not not_4 (not_4_out, IN0);
  not not_5 (not_5_out, S0);
  and and_3 (and_3_out, S1, not_5_out, not_6_out);
  not not_6 (not_6_out, IN1);
  and and_4 (and_4_out, S1, not_7_out, not_8_out);
  not not_7 (not_7_out, S0);
  not not_8 (not_8_out, IN0);
  not not_9 (not_9_out, S1);
  not not_10 (not_10_out, S0);
  not not_11 (not_11_out, IN1);
  not not_12 (not_12_out, S1);
  not not_13 (not_13_out, IN0);
  not not_14 (not_14_out, S0);
  not not_15 (not_15_out, IN0);
  not not_16 (not_16_out, IN1);
  or or_1 (ss1, and_1_out, and_2_out, and_3_out, and_4_out);
  and and_5 (and_5_out, not_9_out, not_10_out, not_11_out, IN0);
  and and_6 (and_6_out, not_12_out, S0, not_13_out);
  and and_7 (and_7_out, S1, not_14_out, not_15_out);
  and and_8 (and_8_out, S1, S0, not_16_out, IN0);
  or or_2 (ss0, and_5_out, and_6_out, and_7_out, and_8_out);
endmodule

module \output  (
  input  [1:0] State,
  input  [1:0] IN,
  output out_3
);

  outputLogic outputlogic_1 (.S1(State[1]), .S0(State[0]), .IN1(IN[1]), .IN0(IN[0]), .Z(out_3));
endmodule

module outputLogic (
  input  S1,
  input  S0,
  input  IN1,
  input  IN0,
  output Z
);

  wire not_1_out;

  and and_1 (Z, S1, S0, not_1_out);
  not not_1 (not_1_out, IN0);
endmodule
