// Logisim project ftoi.circ as structural Verilog: 2 circuits, main circuit main
module main (
  input  [15:0] in_1,
  output [31:0] out_2
);
endmodule

module ftoi (
  input  [15:0] in_1,
  output [31:0] out_2
);

  wire Deformal, Formal, inf_NaN;
  wire [1:0] priority_encoder_1_out;
  wire [4:0] E;
  wire [10:0] multiplexer_1_out;
  wire [31:0] bit_extender_1_out, data, negator_1_out, shifter_1_out, \unsigned ;

  Negator #(.width(32)) negator_1 (.in(\unsigned ), .out(negator_1_out));
  and u_inf_NaN (inf_NaN, in_1[10], in_1[11], in_1[12], in_1[13], in_1[14]);
  nor u_Deformal (Deformal, in_1[10], in_1[11], in_1[12], in_1[13], in_1[14]);
  // Probe on multiplexer_1_out
  Multiplexer #(.width(11), .enable("false")) multiplexer_1 (
    .in0({1'b0, in_1[9:0]}), .in1({1'b1, in_1[9:0]}), .out(multiplexer_1_out), .sel(Formal));
  Multiplexer #(.width(32)) multiplexer_2 (
    .in0(\unsigned ), .in1(negator_1_out), .out(data), .sel(in_1[15]));  // open: en
  nor u_Formal (Formal, inf_NaN, Deformal);
  Subtractor #(.width(5)) subtractor_1 (.a(in_1[14:10]), .b(5'b01111), .out(E));  // open: bin, bout
  assign bit_extender_1_out = {{21{1'b0}}, multiplexer_1_out};  // Bit_Extender bit_extender_1
  // Probe on priority_encoder_1_out
  Priority_Encoder #(.select(2)) priority_encoder_1 (
    .in0(inf_NaN), .in1(Deformal), .in2(Formal), .in3(E[4]), .out(priority_encoder_1_out));  // open: gs, en_out, en_in
  Shifter #(.width(32)) shifter_1 (.in(bit_extender_1_out), .\dist (E), .out(shifter_1_out));
  Multiplexer #(.select(2), .width(32)) multiplexer_3 (
    .in0({32{1'b0}}), .in1({32{1'b0}}), .in2(data), .in3({32{1'b0}}), .out(out_2),
    .sel(priority_encoder_1_out));  // open: en
  assign \unsigned  = {{10{1'b0}}, shifter_1_out[31:10]};  // Bit_Extender bit_extender_2

  // Other names for the same wires on the sheet: frac[9:0] = in_1[9:0]; smallThan1 = E[4]; exp[4:0] = in_1[14:10];
  //   sign = in_1[15]
endmodule
