// Logisim project grf.circ as structural Verilog
module grf (
  input  clk,
  input  reset,
  input  WE,
  input  [4:0] A1,
  input  [4:0] A2,
  input  [4:0] A3,
  input  [31:0] WD,
  output [31:0] RD1,
  output [31:0] RD2
);

  wire w0, w1, w2, w3, w4, w5, w6, w7, w8, w9, w10, w11, w12, w13, w14, w15, w16, w17, w18, w19, w20, w21,
       w22, w23, w24, w25, w26, w27, w28, w29, w30, w31;
  wire [31:0] _0, _1, _2, _3, _4, _5, _6, _7, _8, _9, _10, _11, _12, _13, _14, _15, _16, _17, _18, _19, _20,
       _21, _22, _23, _24, _25, _26, _27, _28, _29, _30, _31;

  Decoder #(.select(5), .disabled(0)) decoder_1 (
    .out0(w0), .out1(w1), .out2(w2), .out3(w3), .out4(w4), .out5(w5), .out6(w6), .out7(w7), .out8(w8),
    .out9(w9), .out10(w10), .out11(w11), .out12(w12), .out13(w13), .out14(w14), .out15(w15), .out16(w16),
    .out17(w17), .out18(w18), .out19(w19), .out20(w20), .out21(w21), .out22(w22), .out23(w23), .out24(w24),
    .out25(w25), .out26(w26), .out27(w27), .out28(w28), .out29(w29), .out30(w30), .out31(w31), .sel(A3),
    .en(WE));
  Register #(.width(32)) u__0 (.Q(_0), .clk(clk), .clr(reset));  // open: D, en
  Register #(.width(32)) u__4 (.D(WD), .en(w4), .Q(_4), .clk(clk), .clr(reset));
  Register #(.width(32)) u__8 (.D(WD), .en(w8), .Q(_8), .clk(clk), .clr(reset));
  Register #(.width(32)) u__12 (.D(WD), .en(w12), .Q(_12), .clk(clk), .clr(reset));
  Register #(.width(32)) u__16 (.D(WD), .en(w16), .Q(_16), .clk(clk), .clr(reset));
  Register #(.width(32)) u__20 (.D(WD), .en(w20), .Q(_20), .clk(clk), .clr(reset));
  Register #(.width(32)) u__24 (.D(WD), .en(w24), .Q(_24), .clk(clk), .clr(reset));
  Register #(.width(32)) u__28 (.D(WD), .en(w28), .Q(_28), .clk(clk), .clr(reset));
  Register #(.width(32)) u__1 (.D(WD), .en(w1), .Q(_1), .clk(clk), .clr(reset));
  Register #(.width(32)) u__5 (.D(WD), .en(w5), .Q(_5), .clk(clk), .clr(reset));
  Register #(.width(32)) u__9 (.D(WD), .en(w9), .Q(_9), .clk(clk), .clr(reset));
  Register #(.width(32)) u__13 (.D(WD), .en(w13), .Q(_13), .clk(clk), .clr(reset));
  Register #(.width(32)) u__17 (.D(WD), .en(w17), .Q(_17), .clk(clk), .clr(reset));
  Register #(.width(32)) u__21 (.D(WD), .en(w21), .Q(_21), .clk(clk), .clr(reset));
  Register #(.width(32)) u__25 (.D(WD), .en(w25), .Q(_25), .clk(clk), .clr(reset));
  Register #(.width(32)) u__29 (.D(WD), .en(w29), .Q(_29), .clk(clk), .clr(reset));
  Register #(.width(32)) u__2 (.D(WD), .en(w2), .Q(_2), .clk(clk), .clr(reset));
  Register #(.width(32)) u__6 (.D(WD), .en(w6), .Q(_6), .clk(clk), .clr(reset));
  Register #(.width(32)) u__10 (.D(WD), .en(w10), .Q(_10), .clk(clk), .clr(reset));
  Register #(.width(32)) u__14 (.D(WD), .en(w14), .Q(_14), .clk(clk), .clr(reset));
  Register #(.width(32)) u__18 (.D(WD), .en(w18), .Q(_18), .clk(clk), .clr(reset));
  Register #(.width(32)) u__22 (.D(WD), .en(w22), .Q(_22), .clk(clk), .clr(reset));
  Register #(.width(32)) u__26 (.D(WD), .en(w26), .Q(_26), .clk(clk), .clr(reset));
  Register #(.width(32)) u__30 (.D(WD), .en(w30), .Q(_30), .clk(clk), .clr(reset));
  Register #(.width(32)) u__3 (.D(WD), .en(w3), .Q(_3), .clk(clk), .clr(reset));
  Register #(.width(32)) u__7 (.D(WD), .en(w7), .Q(_7), .clk(clk), .clr(reset));
  Register #(.width(32)) u__11 (.D(WD), .en(w11), .Q(_11), .clk(clk), .clr(reset));
  Register #(.width(32)) u__15 (.D(WD), .en(w15), .Q(_15), .clk(clk), .clr(reset));
  Register #(.width(32)) u__19 (.D(WD), .en(w19), .Q(_19), .clk(clk), .clr(reset));
  Register #(.width(32)) u__23 (.D(WD), .en(w23), .Q(_23), .clk(clk), .clr(reset));
  Register #(.width(32)) u__27 (.D(WD), .en(w27), .Q(_27), .clk(clk), .clr(reset));
  Register #(.width(32)) u__31 (.D(WD), .en(w31), .Q(_31), .clk(clk), .clr(reset));
  Multiplexer #(.select(5), .width(32), .enable("false")) multiplexer_1 (
    .in0(_0), .in1(_1), .in2(_2), .in3(_3), .in4(_4), .in5(_5), .in6(_6), .in7(_7), .in8(_8), .in9(_9),
    .in10(_10), .in11(_11), .in12(_12), .in13(_13), .in14(_14), .in15(_15), .in16(_16), .in17(_17),
    .in18(_18), .in19(_19), .in20(_20), .in21(_21), .in22(_22), .in23(_23), .in24(_24), .in25(_25),
    .in26(_26), .in27(_27), .in28(_28), .in29(_29), .in30(_30), .in31(_31), .out(RD1), .sel(A1));
  Multiplexer #(.select(5), .width(32), .enable("false")) multiplexer_2 (
    .in0(_0), .in1(_1), .in2(_2), .in3(_3), .in4(_4), .in5(_5), .in6(_6), .in7(_7), .in8(_8), .in9(_9),
    .in10(_10), .in11(_11), .in12(_12), .in13(_13), .in14(_14), .in15(_15), .in16(_16), .in17(_17),
    .in18(_18), .in19(_19), .in20(_20), .in21(_21), .in22(_22), .in23(_23), .in24(_24), .in25(_25),
    .in26(_26), .in27(_27), .in28(_28), .in29(_29), .in30(_30), .in31(_31), .out(RD2), .sel(A2));

  // Other names for the same wires on the sheet: writeData[31:0] = WD
endmodule
