// Logisim project grf_auto.circ as structural Verilog: 1 circuit, main circuit main
module main (
  input  clk,
  input  reset,
  input  WE,
  input  [31:0] WD
);

  wire w1;
  wire [31:0] _1;

  Register #(.width(32)) u__1 (.D(WD), .en(w1), .Q(_1), .clk(clk), .clr(reset));

  // Other names for the same wires on the sheet: writeData[31:0] = WD
endmodule
