// Logisim project navi.circ as structural Verilog
module navigation (
  input  [1:0] dir,
  input  clk,
  input  reset,
  output arrive,
  output hit
);

  wire comparator_1_eq;
  wire [2:0] next_1_nextstate, previous_state, previous_state_q, state;
  wire [7:0] counter_1_q;

  next next_1 (.state(state), .dir(dir), .nextstate(next_1_nextstate));
  Register #(.width(3)) u_previous_state (.D(state), .Q(previous_state_q), .clk(clk), .clr(reset));  // open: en
  // Probe on next_1_nextstate
  Counter counter_1 (.Q(counter_1_q), .clk(clk), .clr(reset));  // open: load, D, count, carry
  Register #(.width(3)) register_1 (.D(next_1_nextstate), .Q(state), .clk(clk), .clr(reset));  // open: en
  Multiplexer #(.width(3), .enable("false")) multiplexer_1 (
    .in0(previous_state_q), .in1(3'b111), .out(previous_state), .sel(comparator_1_eq));
  Comparator comparator_1 (.a({8{1'b0}}), .b(counter_1_q), .eq(comparator_1_eq));  // open: gt, lt
  Register #(.width(3)) register_2 (.D(state));  // open: en, Q, clk, clr
  Comparator #(.width(3)) comparator_2 (.a(state), .b(3'b100), .eq(arrive));  // open: gt, lt
  Comparator #(.width(3)) comparator_3 (.a(previous_state), .b(state), .eq(hit));  // open: gt, lt
endmodule

module next (
  input  [2:0] state,
  input  [1:0] dir,
  output [2:0] nextstate
);

  next_CA next_ca_1 (
    .s2(state[2]), .s1(state[1]), .s0(state[0]), .dirhigh(dir[1]), .dirlow(dir[0]), .ss2(nextstate[2]),
    .ss1(nextstate[1]), .ss0(nextstate[0]));
endmodule

module next_CA (
  input  s2,
  input  s1,
  input  s0,
  input  dirhigh,
  input  dirlow,
  output ss2,
  output ss1,
  output ss0
);

  wire and_1_out, and_2_out, and_3_out, and_4_out, and_5_out, and_6_out, and_7_out, and_8_out, and_9_out,
       and_10_out, and_11_out, not_1_out, not_2_out, not_3_out, not_4_out, not_5_out, not_6_out, not_7_out,
       not_8_out, not_9_out, not_10_out, not_11_out, not_12_out, not_13_out, not_14_out, not_15_out,
       not_16_out, not_17_out;

  not not_1 (not_1_out, s0);
  not not_2 (not_2_out, dirhigh);
  not not_3 (not_3_out, dirlow);
  not not_4 (not_4_out, dirhigh);
  not not_5 (not_5_out, s1);
  not not_6 (not_6_out, dirhigh);
  not not_7 (not_7_out, dirhigh);
  not not_8 (not_8_out, dirlow);
  not not_9 (not_9_out, s0);
  not not_10 (not_10_out, dirhigh);
  not not_11 (not_11_out, s0);
  not not_12 (not_12_out, dirlow);
  not not_13 (not_13_out, s2);
  not not_14 (not_14_out, s1);
  not not_15 (not_15_out, dirhigh);
  not not_16 (not_16_out, dirlow);
  not not_17 (not_17_out, dirlow);
  and and_1 (and_1_out, s1, not_1_out, not_2_out, not_3_out);
  and and_2 (and_2_out, s1, s0, not_4_out, dirlow);
  and and_3 (and_3_out, not_5_out, s0, not_6_out);
  and and_4 (and_4_out, s0, not_7_out, not_8_out);
  and and_5 (and_5_out, s1, not_9_out, not_10_out, dirlow);
  and and_6 (and_6_out, s1, not_11_out, dirhigh, not_12_out);
  and and_7 (and_7_out, s1, s0, dirhigh, dirlow);
  and and_8 (and_8_out, not_13_out, not_14_out, not_15_out, not_16_out);
  and and_9 (and_9_out, s0, dirhigh, dirlow);
  and and_10 (and_10_out, s1, dirhigh, dirlow);
  and and_11 (and_11_out, s1, s0, not_17_out);
  or or_1 (ss2, and_1_out, and_2_out);
  or or_2 (ss1, and_3_out, and_4_out, and_5_out, and_6_out, and_7_out);
  or or_3 (ss0, and_8_out, and_9_out, and_10_out, and_11_out);
endmodule
