// Logisim project swap.circ as structural Verilog: 4 circuits, main circuit main
module main (
  input  [3:0] A,
  input  [3:0] B,
  input  [3:0] C,
  input  [3:0] D,
  output [3:0] _1,
  output [3:0] _2,
  output [3:0] _3,
  output [3:0] _4
);

  _4bit_swap u_4bit_swap_1 ();  // open: in_1, in_2, in_3, out_4, out_5
endmodule

module _1bit_swap (
  input  in_1,
  input  in_2,
  input  in_3,
  output out_4,
  output out_5
);

  wire and_1_out, and_2_out, and_3_out, and_4_out, not_1_out;

  not not_1 (not_1_out, in_3);
  and and_1 (and_1_out, in_1, not_1_out);
  and and_2 (and_2_out, in_2, not_1_out);
  and and_3 (and_3_out, in_1, in_3);
  and and_4 (and_4_out, in_2, in_3);
  or or_1 (out_4, and_1_out, and_4_out);
  or or_2 (out_5, and_2_out, and_3_out);
endmodule

module _4bit_swap (
  input  [3:0] in_1,
  input  [3:0] in_2,
  input  in_3,
  output [3:0] out_4,
  output [3:0] out_5
);

  _1bit_swap u_1bit_swap_1 (.in_1(in_1[0]), .in_2(in_2[0]), .in_3(in_3), .out_4(out_4[0]), .out_5(out_5[0]));
  _1bit_swap u_1bit_swap_2 (.in_1(in_1[1]), .in_2(in_2[1]), .in_3(in_3), .out_4(out_4[1]), .out_5(out_5[1]));
  _1bit_swap u_1bit_swap_3 (.in_1(in_1[2]), .in_2(in_2[2]), .in_3(in_3), .out_4(out_4[2]), .out_5(out_5[2]));
  _1bit_swap u_1bit_swap_4 (.in_1(in_1[3]), .in_2(in_2[3]), .in_3(in_3), .out_4(out_4[3]), .out_5(out_5[3]));
endmodule

module _4bit_sort (
  input  [3:0] A,
  input  [3:0] B,
  input  [3:0] C,
  input  [3:0] D,
  output [3:0] _1,
  output [3:0] _2,
  output [3:0] _3,
  output [3:0] _4
);

  wire comparator_1_gt, comparator_2_gt, comparator_3_gt, comparator_4_gt, comparator_5_gt;
  wire [3:0] n4bit_swap_1_out_4, n4bit_swap_1_out_5, n4bit_swap_2_out_4, n4bit_swap_2_out_5,
       n4bit_swap_3_out_5, n4bit_swap_4_out_4;

  Comparator #(.width(4), .mode("unsigned")) comparator_1 (.a(A), .b(B), .gt(comparator_1_gt));  // open: eq, lt
  Comparator #(.width(4), .mode("unsigned")) comparator_2 (.a(C), .b(D), .gt(comparator_2_gt));  // open: eq, lt
  // Probe on n4bit_swap_2_out_5
  // Probe on n4bit_swap_1_out_4
  _4bit_swap u_4bit_swap_1 (
    .in_1(A), .in_2(B), .in_3(comparator_1_gt), .out_4(n4bit_swap_1_out_4), .out_5(n4bit_swap_1_out_5));
  _4bit_swap u_4bit_swap_2 (
    .in_1(C), .in_2(D), .in_3(comparator_2_gt), .out_4(n4bit_swap_2_out_4), .out_5(n4bit_swap_2_out_5));
  Comparator #(.width(4), .mode("unsigned")) comparator_3 (
    .a(n4bit_swap_1_out_4), .b(n4bit_swap_2_out_4), .gt(comparator_3_gt));  // open: eq, lt
  // Probe on n4bit_swap_1_out_5
  Comparator #(.width(4), .mode("unsigned")) comparator_4 (
    .a(n4bit_swap_1_out_5), .b(n4bit_swap_2_out_5), .gt(comparator_4_gt));  // open: eq, lt
  _4bit_swap u_4bit_swap_3 (
    .in_1(n4bit_swap_1_out_4), .in_2(n4bit_swap_2_out_4), .in_3(comparator_3_gt), .out_4(_1),
    .out_5(n4bit_swap_3_out_5));
  _4bit_swap u_4bit_swap_4 (
    .in_1(n4bit_swap_1_out_5), .in_2(n4bit_swap_2_out_5), .in_3(comparator_4_gt), .out_4(n4bit_swap_4_out_4),
    .out_5(_4));
  Comparator #(.width(4), .mode("unsigned")) comparator_5 (
    .a(n4bit_swap_3_out_5), .b(n4bit_swap_4_out_4), .gt(comparator_5_gt));  // open: eq, lt
  _4bit_swap u_4bit_swap_5 (
    .in_1(n4bit_swap_3_out_5), .in_2(n4bit_swap_4_out_4), .in_3(comparator_5_gt), .out_4(_2), .out_5(_3));
endmodule
