// Logisim project CPU_test_copy.circ as structural Verilog: 11 circuits, main circuit main
module main (
  input  reset,
  output [31:0] out_2,
  output [31:0] out_3,
  output out_4,
  output [4:0] out_5,
  output [31:0] out_6,
  output out_7,
  output [31:0] MemAddr,
  output [31:0] MemData
);

  wire ALUSrc, clk, EXTOp, RAWrite, RegDst, Zero;
  wire [1:0] NPCOp, RegSrc;
  wire [2:0] ALUOp;
  wire [4:0] multiplexer_1_out;
  wire [31:0] EXTImm, LUI32, multiplexer_4_out, npc, PC_4, RD1, ReadData;

  Clock clock_1 (.out(clk));
  IFU ifu_1 (.clk(clk), .reset(reset), .npc(npc), .Instr(out_2), .pc(out_3));
  NPC npc_1 (
    .pc(out_3), .Imm16(out_2[15:0]), .Imm26(out_2[25:0]), .Addr(RD1), .npc(npc), .NPCOp(NPCOp),
    .isEqual(Zero), .PC_4(PC_4));
  Multiplexer #(.width(5), .enable("false")) multiplexer_1 (
    .in0(out_2[15:11]), .in1(out_2[20:16]), .out(multiplexer_1_out), .sel(RegDst));
  Multiplexer #(.width(5), .enable("false")) multiplexer_2 (
    .in0(multiplexer_1_out), .in1({5{1'b1}}), .out(out_5), .sel(RAWrite));
  // Mips_Probe mips_probe_1: pin names not known; wires that end beside it: out_2
  Multiplexer #(.select(2), .width(32), .enable("false")) multiplexer_3 (
    .in0(MemAddr), .in1(ReadData), .in2(LUI32), .in3(PC_4), .out(out_6), .sel(RegSrc));
  EXT ext_1 (.Imm16(out_2[15:0]), .EXTOp(EXTOp), .out_3(EXTImm));
  Mergelo0 mergelo0_1 (.in_1(out_2[15:0]), .out_2(LUI32));
  GRF grf_1 (
    .A1(out_2[25:21]), .A2(out_2[20:16]), .A3(out_5), .WD(out_6), .RD1(RD1), .RD2(MemData), .clk(clk),
    .reset(reset), .WE(out_4));
  Controller controller_1 (
    .Opcode(out_2[31:26]), .funct(out_2[5:0]), .NPCOp(NPCOp), .EXTOp(EXTOp), .RegWrite(out_4),
    .RegSrc(RegSrc), .RegDst(RegDst), .ALUSrc(ALUSrc), .ALUOp(ALUOp), .MemWrite(out_7), .RaWrite(RAWrite));
  // Probe on ALUOp
  // Probe on ALUOp
  // Probe on RD1
  Multiplexer #(.width(32), .enable("false")) multiplexer_4 (
    .in0(MemData), .in1(EXTImm), .out(multiplexer_4_out), .sel(ALUSrc));
  ALU alu_1 (.A(RD1), .B(multiplexer_4_out), .ALUOp(ALUOp), .C(MemAddr), .Zero(Zero));  // open: OverFlow
  DM dm_1 (.clk(clk), .reset(reset), .MemWrite(out_7), .MemAddr(MemAddr), .MemData(MemData), .ReadData(ReadData));
  // Probe on multiplexer_4_out
  // RegisterFile registerfile_1: pin names not known; wires that end beside it: out_4, clk

  // Other names for the same wires on the sheet: C[31:0] = MemAddr; funct[5:0] = out_2[5:0];
  //   Imm16[15:0] = out_2[15:0]; Imm26[25:0] = out_2[25:0]; Instr[31:0] = out_2; shamt[4:0] = out_2[10:6];
  //   rd[4:0] = out_2[15:11]; rt[4:0] = out_2[20:16]; rs[4:0] = out_2[25:21]; opcode[5:0] = out_2[31:26];
  //   MemWrite = out_7; pc[31:0] = out_3; RD2[31:0] = MemData; RegAddr[4:0] = out_5; RegData[31:0] = out_6;
  //   RegWrite = out_4; rst = reset
endmodule

module GRF (
  input  clk,
  input  reset,
  input  WE,
  input  [4:0] A1,
  input  [4:0] A2,
  input  [4:0] A3,
  input  [31:0] WD,
  output [31:0] RD1,
  output [31:0] RD2
);

  wire w0, w1, w2, w3, w4, w5, w6, w7, w8, w9, w10, w11, w12, w13, w14, w15, w16, w17, w18, w19, w20, w21,
       w22, w23, w24, w25, w26, w27, w28, w29, w30, w31;
  wire [31:0] _0, _1, _2, _3, _4, _5, _6, _7, _8, _9, _10, _11, _12, _13, _14, _15, _16, _17, _18, _19, _20,
       _21, _22, _23, _24, _25, _26, _27, _28, _29, _30, _31;

  Decoder #(.select(5), .disabled(0)) decoder_1 (
    .out0(w0), .out1(w1), .out2(w2), .out3(w3), .out4(w4), .out5(w5), .out6(w6), .out7(w7), .out8(w8),
    .out9(w9), .out10(w10), .out11(w11), .out12(w12), .out13(w13), .out14(w14), .out15(w15), .out16(w16),
    .out17(w17), .out18(w18), .out19(w19), .out20(w20), .out21(w21), .out22(w22), .out23(w23), .out24(w24),
    .out25(w25), .out26(w26), .out27(w27), .out28(w28), .out29(w29), .out30(w30), .out31(w31), .sel(A3),
    .en(WE));
  Register #(.width(32)) u__0 (.Q(_0), .clk(clk), .clr(reset));  // open: D, en
  Register #(.width(32)) u__4 (.D(WD), .en(w4), .Q(_4), .clk(clk), .clr(reset));
  Register #(.width(32)) u__8 (.D(WD), .en(w8), .Q(_8), .clk(clk), .clr(reset));
  Register #(.width(32)) u__12 (.D(WD), .en(w12), .Q(_12), .clk(clk), .clr(reset));
  Register #(.width(32)) u__16 (.D(WD), .en(w16), .Q(_16), .clk(clk), .clr(reset));
  Register #(.width(32)) u__20 (.D(WD), .en(w20), .Q(_20), .clk(clk), .clr(reset));
  Register #(.width(32)) u__24 (.D(WD), .en(w24), .Q(_24), .clk(clk), .clr(reset));
  Register #(.width(32)) u__28 (.D(WD), .en(w28), .Q(_28), .clk(clk), .clr(reset));
  Register #(.width(32)) u__1 (.D(WD), .en(w1), .Q(_1), .clk(clk), .clr(reset));
  Register #(.width(32)) u__5 (.D(WD), .en(w5), .Q(_5), .clk(clk), .clr(reset));
  Register #(.width(32)) u__9 (.D(WD), .en(w9), .Q(_9), .clk(clk), .clr(reset));
  Register #(.width(32)) u__13 (.D(WD), .en(w13), .Q(_13), .clk(clk), .clr(reset));
  Register #(.width(32)) u__17 (.D(WD), .en(w17), .Q(_17), .clk(clk), .clr(reset));
  Register #(.width(32)) u__21 (.D(WD), .en(w21), .Q(_21), .clk(clk), .clr(reset));
  Register #(.width(32)) u__25 (.D(WD), .en(w25), .Q(_25), .clk(clk), .clr(reset));
  Register #(.width(32)) u__29 (.D(WD), .en(w29), .Q(_29), .clk(clk), .clr(reset));
  Register #(.width(32)) u__2 (.D(WD), .en(w2), .Q(_2), .clk(clk), .clr(reset));
  Register #(.width(32)) u__6 (.D(WD), .en(w6), .Q(_6), .clk(clk), .clr(reset));
  Register #(.width(32)) u__10 (.D(WD), .en(w10), .Q(_10), .clk(clk), .clr(reset));
  Register #(.width(32)) u__14 (.D(WD), .en(w14), .Q(_14), .clk(clk), .clr(reset));
  Register #(.width(32)) u__18 (.D(WD), .en(w18), .Q(_18), .clk(clk), .clr(reset));
  Register #(.width(32)) u__22 (.D(WD), .en(w22), .Q(_22), .clk(clk), .clr(reset));
  Register #(.width(32)) u__26 (.D(WD), .en(w26), .Q(_26), .clk(clk), .clr(reset));
  Register #(.width(32)) u__30 (.D(WD), .en(w30), .Q(_30), .clk(clk), .clr(reset));
  Register #(.width(32)) u__3 (.D(WD), .en(w3), .Q(_3), .clk(clk), .clr(reset));
  Register #(.width(32)) u__7 (.D(WD), .en(w7), .Q(_7), .clk(clk), .clr(reset));
  Register #(.width(32)) u__11 (.D(WD), .en(w11), .Q(_11), .clk(clk), .clr(reset));
  Register #(.width(32)) u__15 (.D(WD), .en(w15), .Q(_15), .clk(clk), .clr(reset));
  Register #(.width(32)) u__19 (.D(WD), .en(w19), .Q(_19), .clk(clk), .clr(reset));
  Register #(.width(32)) u__23 (.D(WD), .en(w23), .Q(_23), .clk(clk), .clr(reset));
  Register #(.width(32)) u__27 (.D(WD), .en(w27), .Q(_27), .clk(clk), .clr(reset));
  Register #(.width(32)) u__31 (.D(WD), .en(w31), .Q(_31), .clk(clk), .clr(reset));
  Multiplexer #(.select(5), .width(32), .enable("false")) multiplexer_1 (
    .in0(_0), .in1(_1), .in2(_2), .in3(_3), .in4(_4), .in5(_5), .in6(_6), .in7(_7), .in8(_8), .in9(_9),
    .in10(_10), .in11(_11), .in12(_12), .in13(_13), .in14(_14), .in15(_15), .in16(_16), .in17(_17),
    .in18(_18), .in19(_19), .in20(_20), .in21(_21), .in22(_22), .in23(_23), .in24(_24), .in25(_25),
    .in26(_26), .in27(_27), .in28(_28), .in29(_29), .in30(_30), .in31(_31), .out(RD1), .sel(A1));
  Multiplexer #(.select(5), .width(32), .enable("false")) multiplexer_2 (
    .in0(_0), .in1(_1), .in2(_2), .in3(_3), .in4(_4), .in5(_5), .in6(_6), .in7(_7), .in8(_8), .in9(_9),
    .in10(_10), .in11(_11), .in12(_12), .in13(_13), .in14(_14), .in15(_15), .in16(_16), .in17(_17),
    .in18(_18), .in19(_19), .in20(_20), .in21(_21), .in22(_22), .in23(_23), .in24(_24), .in25(_25),
    .in26(_26), .in27(_27), .in28(_28), .in29(_29), .in30(_30), .in31(_31), .out(RD2), .sel(A2));

  // Other names for the same wires on the sheet: writeData[31:0] = WD
endmodule

module IFU (
  input  clk,
  input  reset,
  input  [31:0] npc,
  output [31:0] Instr,
  output [31:0] pc
);

  wire [31:0] register_1_q, subtractor_1_out;

  Subtractor #(.width(32)) subtractor_1 (
    .a({npc[31:2], 2'b00}), .b(32'h3000), .out(subtractor_1_out));  // open: bin, bout
  Register #(.width(32)) register_1 (.D(subtractor_1_out), .Q(register_1_q), .clk(clk), .clr(reset));  // open: en
  // Probe on subtractor_1_out
  ROM #(.addrWidth(12), .dataWidth(32)) rom_1 (.addr(register_1_q[13:2]), .data(Instr));  // open: sel
  Adder #(.width(32)) adder_1 (.a(register_1_q), .b(32'h3000), .out(pc));  // open: cin, cout

  // Other names for the same wires on the sheet: rst = reset

  // Notes on the sheet:
  //   contents of rom_1 (hex, n*v repeats v):
  //   3c010000 34210001 3c02ffff 3442ffff 3c037fff 3463ffff 3c041000 34840000 222820 213020 413822 224022
  //   612820 823020 623822 814022 3c050000 34a52ffc ac030000 ac030004 ac040008 aca3fffc aca4fff8 8c000000
  //   8c060000 8c060004 8c060008 8ca6fffc 8ca6fff8 10420002 1294820 1021fffe 1023fffd 1063fffb
endmodule

module ALU (
  input  [31:0] A,
  input  [31:0] B,
  input  [2:0] ALUOp,
  output [31:0] C,
  output Zero,
  output OverFlow
);

  wire [31:0] adder_1_out, and_1_out, or_1_out, SUB;

  assign or_1_out = A | B;  // OR_Gate or_1, 32 bits wide
  assign and_1_out = A & B;  // AND_Gate and_1, 32 bits wide
  Adder #(.width(32)) adder_1 (.a(A), .b(B), .out(adder_1_out));  // open: cin, cout
  Subtractor #(.width(32)) subtractor_1 (.a(A), .b(B), .out(SUB));  // open: bin, bout
  Multiplexer #(.select(3), .width(32)) multiplexer_1 (
    .in0(adder_1_out), .in1(SUB), .in2(or_1_out), .in3(and_1_out), .out(C), .sel(ALUOp));  // open: in4, in5, in6, in7, en
  Comparator #(.width(32)) comparator_1 (.a(SUB), .b({32{1'b0}}), .eq(Zero));  // open: gt, lt

  assign OverFlow = 1'b0;

  // Other names for the same wires on the sheet: op[2:0] = ALUOp
endmodule

module DM (
  input  clk,
  input  reset,
  input  MemWrite,
  input  [31:0] MemAddr,
  input  [31:0] MemData,
  output [31:0] ReadData
);

  wire not_1_out;

  not not_1 (not_1_out, MemWrite);
  RAM #(.addrWidth(12), .dataWidth(32), .bus("separate")) ram_1 (
    .addr(MemAddr[13:2]), .din(MemData), .data(ReadData), .str(MemWrite), .clk(clk), .ld(not_1_out),
    .clr(reset));  // open: sel

  // Other names for the same wires on the sheet: rst = reset; WE = MemWrite
endmodule

module EXT (
  input  [15:0] Imm16,
  input  EXTOp,
  output [31:0] out_3
);

  wire [31:0] bit_extender_1_out, bit_extender_2_out;

  assign bit_extender_1_out = {{16{1'b0}}, Imm16};  // Bit_Extender bit_extender_1
  assign bit_extender_2_out = {{16{Imm16[15]}}, Imm16};  // Bit_Extender bit_extender_2
  Multiplexer #(.width(32)) multiplexer_1 (
    .in0(bit_extender_1_out), .in1(bit_extender_2_out), .out(out_3), .sel(EXTOp));  // open: en
endmodule

module NPC (
  input  [1:0] NPCOp,
  input  isEqual,
  input  [31:0] pc,
  input  [15:0] Imm16,
  input  [25:0] Imm26,
  input  [31:0] Addr,
  output [31:0] npc,
  output [31:0] PC_4
);

  wire [31:0] adder_2_out, bit_extender_1_out, branch;

  assign bit_extender_1_out = {{14{Imm16[15]}}, {Imm16, 2'b00}};  // Bit_Extender bit_extender_1
  Adder #(.width(32)) adder_1 (.a({pc[31:2], 2'b00}), .b(32'h4), .out(PC_4));  // open: cin, cout
  Adder #(.width(32)) adder_2 (.a(PC_4), .b(bit_extender_1_out), .out(adder_2_out));  // open: cin, cout
  // Probe on {pc[31:28], Imm26, 2'b00}
  // Probe on PC_4
  // Probe on adder_2_out
  Multiplexer #(.width(32), .enable("false")) multiplexer_1 (
    .in0(PC_4), .in1(adder_2_out), .out(branch), .sel(isEqual));
  Multiplexer #(.select(2), .width(32)) multiplexer_2 (
    .in0(PC_4), .in1(branch), .in2({pc[31:28], Imm26, 2'b00}), .in3(Addr), .out(npc), .sel(NPCOp));  // open: en

  // Other names for the same wires on the sheet: PC_imm26_00[31:2] = {pc[31:28], Imm26}
endmodule

module Mergelo0 (
  input  [15:0] in_1,
  output [31:0] out_2
);


  assign out_2 = {in_1, {16{1'b0}}};
endmodule

module Controller (
  input  [5:0] Opcode,
  input  [5:0] funct,
  output [1:0] NPCOp,
  output EXTOp,
  output RegWrite,
  output [1:0] RegSrc,
  output RegDst,
  output ALUSrc,
  output [2:0] ALUOp,
  output MemWrite,
  output RaWrite
);

  wire add, ADD_out, Addr_out, ALU_out, beq, DM_out, imm16_out, imm26_out, jal, jr, lui, LUI_out, lw, nop,
       not_1_out, not_2_out, not_3_out, not_4_out, not_5_out, not_6_out, not_7_out, not_8_out, not_9_out,
       not_10_out, not_11_out, not_12_out, or_2_out, or_3_out, or_4_out, OR_out, ori, PC_4_out, R_type, sub,
       SUB_out, sw;

  not not_1 (not_1_out, funct[5]);
  not not_2 (not_2_out, Opcode[5]);
  not not_3 (not_3_out, funct[4]);
  not not_4 (not_4_out, Opcode[4]);
  not not_5 (not_5_out, funct[3]);
  not not_6 (not_6_out, funct[2]);
  not not_7 (not_7_out, Opcode[2]);
  not not_8 (not_8_out, Opcode[3]);
  not not_9 (not_9_out, funct[1]);
  not not_10 (not_10_out, Opcode[1]);
  not not_11 (not_11_out, funct[0]);
  not not_12 (not_12_out, Opcode[0]);
  and and_1 (R_type, not_12_out, not_10_out, not_7_out, not_8_out, not_4_out, not_2_out);
  and and_2 (ori, not_2_out, not_4_out, Opcode[3], Opcode[2], not_10_out, Opcode[0]);
  and and_3 (lw, Opcode[5], not_4_out, not_8_out, not_7_out, Opcode[1], Opcode[0]);
  and and_4 (sw, Opcode[5], not_4_out, Opcode[3], not_7_out, Opcode[1], Opcode[0]);
  and and_5 (beq, not_2_out, not_4_out, not_8_out, Opcode[2], not_10_out, not_12_out);
  and and_6 (lui, not_2_out, not_4_out, Opcode[3], Opcode[2], Opcode[1], Opcode[0]);
  and and_7 (jal, not_2_out, not_4_out, not_8_out, not_7_out, Opcode[1], Opcode[0]);
  and and_8 (add, R_type, funct[5], not_3_out, not_5_out, not_6_out, not_9_out, not_11_out);
  and and_9 (sub, R_type, funct[5], not_3_out, not_5_out, not_6_out, funct[1], not_11_out);
  and and_10 (nop, R_type, not_1_out, not_3_out, not_5_out, not_6_out, not_9_out, not_11_out);
  and and_11 (jr, not_1_out, not_3_out, funct[3], not_6_out, not_9_out, not_11_out);
  or PC_4 (PC_4_out, ori, lw, sw, lui, add, sub, nop);
  buf imm16 (imm16_out, beq);  // OR_Gate
  buf imm26 (imm26_out, jal);  // OR_Gate
  buf Addr (Addr_out, jr);  // OR_Gate
  or SignExt (EXTOp, sw, lw);
  or u_RegWrite (RegWrite, ori, lw, lui, add, sub);
  or ALU (ALU_out, add, sub, ori);
  buf DM (DM_out, lw);  // OR_Gate
  buf u_LUI (LUI_out, lui);  // OR_Gate
  or u_RegDst (RegDst, ori, lw, lui);
  or u_ALUSrc (ALUSrc, ori, lw, sw);
  or u_ADD (ADD_out, add, lw, sw);
  buf u_SUB (SUB_out, sub);  // OR_Gate
  buf OR (OR_out, ori);  // OR_Gate
  // OR_Gate AND_12 is placed but not wired
  buf u_MemWrite (MemWrite, sw);  // OR_Gate
  buf u_RaWrite (RaWrite, jal);  // OR_Gate
  Priority_Encoder #(.select(2), .disabled(0)) priority_encoder_1 (
    .in0(PC_4_out), .in1(imm16_out), .in2(imm26_out), .in3(Addr_out), .out(NPCOp), .en_in(or_2_out));  // open: gs, en_out
  or or_2 (or_2_out, imm16_out, imm26_out, PC_4_out, Addr_out);
  Priority_Encoder #(.select(2), .disabled(0)) priority_encoder_2 (
    .in0(ALU_out), .in1(DM_out), .in2(LUI_out), .out(RegSrc), .en_in(or_3_out));  // open: in3, gs, en_out
  or or_3 (or_3_out, ALU_out, DM_out, LUI_out);
  Priority_Encoder #(.disabled(0)) priority_encoder_3 (
    .in0(ADD_out), .in1(SUB_out), .in2(OR_out), .out(ALUOp), .en_in(or_4_out));  // open: in3, in4, in5, in6, in7, gs, en_out
  or or_4 (or_4_out, ADD_out, SUB_out, OR_out);

  // Other names for the same wires on the sheet: f0 = funct[0]; f1 = funct[1]; f2 = funct[2]; f3 = funct[3];
  //   f4 = funct[4]; f5 = funct[5]; op0 = Opcode[0]; op1 = Opcode[1]; op2 = Opcode[2]; op3 = Opcode[3];
  //   op4 = Opcode[4]; op5 = Opcode[5]
endmodule

module fetcher (
  input  [31:0] \byte ,
  input  [31:0] memword,
  output [31:0] out_3
);

  wire [31:0] bit_extender_1_out, bit_extender_2_out, bit_extender_3_out, bit_extender_4_out;

  assign bit_extender_1_out = {{24{1'b0}}, memword[7:0]};  // Bit_Extender bit_extender_1
  assign bit_extender_2_out = {{24{1'b0}}, memword[15:8]};  // Bit_Extender bit_extender_2
  assign bit_extender_3_out = {{24{1'b0}}, memword[23:16]};  // Bit_Extender bit_extender_3
  assign bit_extender_4_out = {{24{1'b0}}, memword[31:24]};  // Bit_Extender bit_extender_4
  Multiplexer #(.select(2), .width(32)) multiplexer_1 (
    .in0(bit_extender_1_out), .in1(bit_extender_2_out), .in2(bit_extender_3_out), .in3(bit_extender_4_out),
    .out(out_3), .sel(\byte [1:0]));  // open: en
  // Probe on nothing

  // Other names for the same wires on the sheet: byte_t[1:0] = \byte [1:0]; hw = \byte [1]
endmodule

module fetcher1 (
  input  [31:0] \byte ,
  input  [31:0] memword,
  output [31:0] out_3
);

  wire [4:0] multiplexer_2_out;
  wire [7:0] multiplexer_1_out;
  wire [31:0] bit_extender_1_out;

  Multiplexer #(.select(2), .width(8)) multiplexer_1 (
    .in0(memword[7:0]), .in1(memword[15:8]), .in2(memword[23:16]), .in3(memword[31:24]),
    .out(multiplexer_1_out), .sel(\byte [1:0]));  // open: en
  assign bit_extender_1_out = {{24{1'b0}}, multiplexer_1_out};  // Bit_Extender bit_extender_1
  Multiplexer #(.select(2), .width(5)) multiplexer_2 (
    .in0({5{1'b0}}), .in1(5'b01000), .in2(5'b10000), .in3(5'b11000), .out(multiplexer_2_out),
    .sel(\byte [1:0]));  // open: en
  Shifter #(.width(32)) shifter_1 (.in(bit_extender_1_out), .\dist (multiplexer_2_out), .out(out_3));
endmodule
